# Fritzing sketch Rover_5_interconnects (saved by Fritzing 0.9.1b)
breadboards: 1

parts:
  Part1 = Arduino Uno (Rev3)
  VCC1 = Battery block 9V  # not connected
  Raspberry_Pi2 = Raspberry Pi B+

nets:
  GND: Part1.GND, Raspberry_Pi2.GPIO11, Raspberry_Pi2.GND
  N1: Part1.D0/RX, Raspberry_Pi2.GPIO14
  N2: Part1.D1/TX, Raspberry_Pi2.GPIO15
  VIN: Part1.VIN, Raspberry_Pi2.5V

notes:
  Breadboard Represents the motor driver board.
  Cyan wires are PWM and orange are direction.
  The 9v battery represents our motor battery (fritzing doesnt have NiMH cells lol)
  Left most breadboard power rails +/- are our logic rails, connected from +5v arduino to +VCC on the motor driver. And GND on arduino to GND/-VCC on the motor driver.
  Right most rails are our battery connections on the motor driver. Positive battery lead goes to +Bat negative lead to -Bat/GND.
  The motor driver also needs a GND pin for each motor channel control signal. We can now provide this from our protoshield which gives us five additional GND connections. Current (CUR) pins are not connected for now.
  Connections:
  Arduino 0 (RX) to Pi TX
  Arduino 1 (TX) to Pi RX
  Arduino 2 to Channel 2 direction (DIR)
  Arduino 3 to Channel 4 PWM
  Arduino 4 to Channel 1 direction (DIR)
  Arduino 5 to Channel 1 PWM
  Arduino 6 to Channel 3 PWM
  Arduino 7 to Channel 3 direction (DIR)
  Arduino 8 not connected
  Arduino 9 to Channel 2 PWM
  Arduino 10 to Channel 4 direction (DIR)
  Arduino 11 not connected
  Arduino 12 not connected
  Arduino 13 not connected
  All analogs not connected
  Arduino Vin to Pi +5V
  Arduino GND to Pi GND
